# Fritzing sketch voiceMask (saved by Fritzing 0.9.3b)
breadboards: 1

parts:
  元件1 = Arduino Nano (Rev3.0)
  R1 = Temperature Sensor (Thermistor) [thermistor_type=NTC package=THT]
  R2 = Resistor [tolerance=±5% resistance=10k package="2512 [SMD]"]
  元件2 = LED Matrix - Serial Interface - Red/Green/Blue
  S1 = Pushbutton [package="[THT]"]
  S2 = Pushbutton [package="[THT]"]
  S3 = Pushbutton [package="[THT]"]
  元件3 = Breakout Board for Electret Microphone
  VCC1 = Battery block 9V
  U1 = DC-DC_CONVERTER [package=dc-dc_converter]

nets:
  GND: 元件1.GND, R2.Pin_1, S1.Pin_1, S1.Pin_2, S2.Pin_1, S2.Pin_2, S3.Pin_1, S3.Pin_2, 元件3.GND, VCC1.-, U1.GND1
  N1: 元件1.D2, S2.Pin_3, S2.Pin_4
  N2: 元件1.D3, S1.Pin_3, S1.Pin_4
  N3: 元件1.D4, S3.Pin_3, S3.Pin_4
  VCC: 元件1.D6, 元件2.VCC, 元件3.VCC, U1.VOUT
  VIN: 元件1.VIN, VCC1.+, U1.VIN
  N4: 元件1.5V, R1.pin_0
  N5: 元件1.A7, 元件3.AUD
  N6: 元件1.A6, R1.pin_1, R2.Pin_0
  GND_2: 元件2.GND, U1.GND2

notes:
  由于部分元件没有在该软件中找到对应的，故图中部分元件只是接线对应，但和实物略有不符
  使用的是8x8 WS2812点阵，其中的数据控制引脚为D6
  固定5V降压模块
